# Fritzing sketch ControlUnit Sheild for MegaPro RoboDyn EVNikolaProject PCB (saved by Fritzing 0.9.3b)
circuit board: 10.4823cm x 8.12505cm
breadboards: 1

parts:
  D1 = Rectifier Diode [part_number=1N4001 package="300 mil [THT]"]  # not connected
  J2 = JST-VHR-3N [part_number=JST-VHR-3N package=THT]
  J3 = JST-VHR-3N [part_number=JST-VHR-3N package=THT]
  Q1 = MOSFET-NCHANNEL [package=to220v]  # not connected
  Q2 = MOSFET-NCHANNEL [package=to220v]  # not connected
  Q3 = MOSFET-NCHANNEL [package=to220v]  # not connected

nets:
  N1: J2.pin1, J2.pin_4, J3.pin1, J3.pin_4

notes:
  I2C(nano)
  UART(Nextion)
  WH.SW1
  WH.SW2
  uSW4
  SW3
  SW4
  Res. 5k (8+GND)
  Res. 5k (4+GND)
  2pSW
  uSW1
  uSW2
  SW2
  uSW3
  SW1
  REZ
  5V
  to 16-channel Relay
  PWM
